// Logisim project Apollo-8.circ as structural Verilog: 54 circuits, main circuit UI
module OneBitAdder (
  input  A,
  input  B,
  input  Carry_in,
  output Sum,
  output Carry_out
);

  wire and_gate_1_out_3, and_gate_2_out_3, xor_1_out;

  XOR xor_1 (.INPUT_1(A), .INPUT_2(B), .OUT(xor_1_out));
  AND_Gate and_gate_1 (.in_1(A), .in_2(B), .out_3(and_gate_1_out_3));
  XOR xor_2 (.INPUT_1(xor_1_out), .INPUT_2(Carry_in), .OUT(Sum));
  AND_Gate and_gate_2 (.in_1(xor_1_out), .in_2(Carry_in), .out_3(and_gate_2_out_3));
  OR_Gate or_gate_1 (.in_1(and_gate_1_out_3), .in_2(and_gate_2_out_3), .out_3(Carry_out));

  // Notes on the sheet:
  //   XOR
  //   AND
  //   Intermediate Sum
  //   Carry out (A+B)
  //   XOR
  //   AND
  //   OR
endmodule

module TwobitFullAdder (
  input  A1,
  input  A0,
  input  B1,
  input  B0,
  input  Carry_in,
  output Carry_Out,
  output S1,
  output S0
);

  wire onebitadder_1_carry_out;

  OneBitAdder onebitadder_1 (.A(A0), .B(B0), .Sum(S0), .Carry_out(onebitadder_1_carry_out), .Carry_in(Carry_in));
  OneBitAdder onebitadder_2 (.A(A1), .B(B1), .Sum(S1), .Carry_out(Carry_Out), .Carry_in(onebitadder_1_carry_out));
endmodule

module FourBitAdder (
  input  A3,
  input  A2,
  input  A1,
  input  A0,
  input  B3,
  input  B2,
  input  B1,
  input  B0,
  input  Carry_in,
  output Carry_out,
  output S3,
  output S2,
  output S1,
  output S0
);

  wire onebitadder_1_carry_out, onebitadder_2_carry_out, onebitadder_3_carry_out;

  OneBitAdder onebitadder_1 (.A(A0), .B(B0), .Sum(S0), .Carry_out(onebitadder_1_carry_out), .Carry_in(Carry_in));
  OneBitAdder onebitadder_2 (
    .A(A1), .B(B1), .Sum(S1), .Carry_out(onebitadder_2_carry_out), .Carry_in(onebitadder_1_carry_out));
  OneBitAdder onebitadder_3 (
    .A(A2), .B(B2), .Sum(S2), .Carry_out(onebitadder_3_carry_out), .Carry_in(onebitadder_2_carry_out));
  OneBitAdder onebitadder_4 (.A(A3), .B(B3), .Sum(S3), .Carry_out(Carry_out), .Carry_in(onebitadder_3_carry_out));
endmodule

// Adder
module EightbitAdder_Using_MAJ___ODD (
  input  [7:0] A,
  input  [7:0] B,
  input  Carry_in,
  output Carry_out,
  output [7:0] Sum
);

  wire maj_1_out_4, maj_2_out_4, maj_3_out_4, maj_4_out_4, maj_5_out_4, maj_6_out_4, maj_7_out_4;

  MAJ maj_1 (.A(A[0]), .B(B[0]), .C(Carry_in), .out_4(maj_1_out_4));
  ODD odd_1 (.A(A[0]), .B(B[0]), .out_4(Sum[0]), .in_3(Carry_in));
  MAJ maj_2 (.A(A[1]), .B(B[1]), .C(maj_1_out_4), .out_4(maj_2_out_4));
  ODD odd_2 (.A(A[1]), .B(B[1]), .out_4(Sum[1]), .in_3(maj_1_out_4));
  MAJ maj_3 (.A(A[2]), .B(B[2]), .C(maj_2_out_4), .out_4(maj_3_out_4));
  ODD odd_3 (.A(A[2]), .B(B[2]), .out_4(Sum[2]), .in_3(maj_2_out_4));
  MAJ maj_4 (.A(A[3]), .B(B[3]), .C(maj_3_out_4), .out_4(maj_4_out_4));
  ODD odd_4 (.A(A[3]), .B(B[3]), .out_4(Sum[3]), .in_3(maj_3_out_4));
  MAJ maj_5 (.A(A[4]), .B(B[4]), .C(maj_4_out_4), .out_4(maj_5_out_4));
  ODD odd_5 (.A(A[4]), .B(B[4]), .out_4(Sum[4]), .in_3(maj_4_out_4));
  MAJ maj_6 (.A(A[5]), .B(B[5]), .C(maj_5_out_4), .out_4(maj_6_out_4));
  ODD odd_6 (.A(A[5]), .B(B[5]), .out_4(Sum[5]), .in_3(maj_5_out_4));
  MAJ maj_7 (.A(A[6]), .B(B[6]), .C(maj_6_out_4), .out_4(maj_7_out_4));
  ODD odd_7 (.A(A[6]), .B(B[6]), .out_4(Sum[6]), .in_3(maj_6_out_4));
  MAJ maj_8 (.A(A[7]), .B(B[7]), .C(maj_7_out_4), .out_4(Carry_out));
  ODD odd_8 (.A(A[7]), .B(B[7]), .out_4(Sum[7]), .in_3(maj_7_out_4));
endmodule

module Demultiplexor (
  input  X,
  input  _3rd_bit,
  input  _2nd_bit,
  input  _1st_bit,
  output M7,
  output out_6,
  output M6,
  output out_8,
  output M5,
  output out_10,
  output M4,
  output out_12,
  output M3,
  output out_14,
  output M2,
  output out_16,
  output M1,
  output out_18,
  output M0,
  output out_20
);

  Decoder decoder_1 (
    .A(_3rd_bit), .B(_2nd_bit), .C(_1st_bit), .D7(out_6), .D6(out_8), .D5(out_10), .D4(out_12), .D3(out_14),
    .D2(out_16), .D1(out_18), .D0(out_20));
  AND_Gate and_gate_1 (.in_1(X), .in_2(out_6), .out_3(M7));
  AND_Gate and_gate_2 (.in_1(X), .in_2(out_8), .out_3(M6));
  AND_Gate and_gate_3 (.in_1(X), .in_2(out_10), .out_3(M5));
  AND_Gate and_gate_4 (.in_1(X), .in_2(out_12), .out_3(M4));
  AND_Gate and_gate_5 (.in_1(X), .in_2(out_14), .out_3(M3));
  AND_Gate and_gate_6 (.in_1(X), .in_2(out_16), .out_3(M2));
  AND_Gate and_gate_7 (.in_1(X), .in_2(out_18), .out_3(M1));
  AND_Gate and_gate_8 (.in_1(X), .in_2(out_20), .out_3(M0));

  // Notes on the sheet:
  //   X: pull=down
endmodule

module Decoder (
  input  A,
  input  B,
  input  C,
  output D7,
  output D6,
  output D5,
  output D4,
  output D3,
  output D2,
  output D1,
  output D0
);

  wire not_1_out, not_2_out, not_3_out;

  not not_1 (not_1_out, C);
  not not_2 (not_2_out, B);
  not not_3 (not_3_out, A);
  AND3 and3_1 (.in_1(A), .in_2(B), .in_3(C), .out_4(D7));
  AND3 and3_2 (.in_1(A), .in_2(B), .in_3(not_1_out), .out_4(D6));
  AND3 and3_3 (.in_1(A), .in_2(not_2_out), .in_3(C), .out_4(D5));
  AND3 and3_4 (.in_1(A), .in_2(not_2_out), .in_3(not_1_out), .out_4(D4));
  AND3 and3_5 (.in_1(not_3_out), .in_2(B), .in_3(C), .out_4(D3));
  AND3 and3_6 (.in_1(not_3_out), .in_2(B), .in_3(not_1_out), .out_4(D2));
  AND3 and3_7 (.in_1(not_3_out), .in_2(not_2_out), .in_3(C), .out_4(D1));
  AND3 and3_8 (.in_1(not_3_out), .in_2(not_2_out), .in_3(not_1_out), .out_4(D0));
endmodule

// DD
module DD_4_to_32 (
  input  X,
  input  A3,
  input  A2,
  input  A1,
  input  A0,
  output out_6,
  output out_7,
  output out_8,
  output out_9,
  output out_10,
  output out_11,
  output out_12,
  output out_13,
  output out_14,
  output out_15,
  output out_16,
  output out_17,
  output out_18,
  output out_19,
  output out_20,
  output out_21,
  output out_22,
  output out_23,
  output out_24,
  output out_25,
  output out_26,
  output out_27,
  output out_28,
  output out_29,
  output out_30,
  output out_31,
  output out_32,
  output out_33,
  output out_34,
  output out_35,
  output out_36,
  output out_37
);

  Decoder_4_to_16 decoder_4_to_16_1 (
    .A3(A3), .A2(A2), .A1(A1), .A0(A0), .DF(out_37), .DE(out_35), .DD(out_33), .DC(out_31), .DB(out_29),
    .DA(out_27), .D9(out_25), .D8(out_23), .D7(out_21), .D6(out_19), .D5(out_17), .D4(out_15), .D3(out_13),
    .D2(out_11), .D1(out_9), .D0(out_7));
  AND_Gate and_gate_1 (.in_1(X), .in_2(out_7), .out_3(out_6));
  AND_Gate and_gate_2 (.in_1(X), .in_2(out_9), .out_3(out_8));
  AND_Gate and_gate_3 (.in_1(X), .in_2(out_11), .out_3(out_10));
  AND_Gate and_gate_4 (.in_1(X), .in_2(out_13), .out_3(out_12));
  AND_Gate and_gate_5 (.in_1(X), .in_2(out_15), .out_3(out_14));
  AND_Gate and_gate_6 (.in_1(X), .in_2(out_17), .out_3(out_16));
  AND_Gate and_gate_7 (.in_1(X), .in_2(out_19), .out_3(out_18));
  AND_Gate and_gate_8 (.in_1(X), .in_2(out_21), .out_3(out_20));
  AND_Gate and_gate_9 (.in_1(X), .in_2(out_23), .out_3(out_22));
  AND_Gate and_gate_10 (.in_1(X), .in_2(out_25), .out_3(out_24));
  AND_Gate and_gate_11 (.in_1(X), .in_2(out_27), .out_3(out_26));
  AND_Gate and_gate_12 (.in_1(X), .in_2(out_29), .out_3(out_28));
  AND_Gate and_gate_13 (.in_1(X), .in_2(out_31), .out_3(out_30));
  AND_Gate and_gate_14 (.in_1(X), .in_2(out_33), .out_3(out_32));
  AND_Gate and_gate_15 (.in_1(X), .in_2(out_35), .out_3(out_34));
  AND_Gate and_gate_16 (.in_1(X), .in_2(out_37), .out_3(out_36));

  // Notes on the sheet:
  //   X: pull=down
endmodule

// Decoder
module Decoder_4_to_16 (
  input  A3,
  input  A2,
  input  A1,
  input  A0,
  output DF,
  output DE,
  output DD,
  output DC,
  output DB,
  output DA,
  output D9,
  output D8,
  output D7,
  output D6,
  output D5,
  output D4,
  output D3,
  output D2,
  output D1,
  output D0
);

  wire not_small_1_y, not_small_2_y, not_small_3_y, not_small_4_y;

  NOT_Small not_small_1 (.Y(not_small_1_y), .X(A3));
  NOT_Small not_small_2 (.Y(not_small_2_y), .X(A2));
  NOT_Small not_small_3 (.Y(not_small_3_y), .X(A1));
  NOT_Small not_small_4 (.Y(not_small_4_y), .X(A0));
  AND4 and4_1 (.in_1(not_small_1_y), .in_2(not_small_2_y), .in_3(not_small_3_y), .in_4(not_small_4_y), .out_5(D0));
  AND4 and4_2 (.in_1(not_small_1_y), .in_2(not_small_2_y), .in_3(not_small_3_y), .in_4(A0), .out_5(D1));
  AND4 and4_3 (.in_1(not_small_1_y), .in_2(not_small_2_y), .in_3(A1), .in_4(not_small_4_y), .out_5(D2));
  AND4 and4_4 (.in_1(not_small_1_y), .in_2(not_small_2_y), .in_3(A1), .in_4(A0), .out_5(D3));
  AND4 and4_5 (.in_1(not_small_1_y), .in_2(A2), .in_3(not_small_3_y), .in_4(not_small_4_y), .out_5(D4));
  AND4 and4_6 (.in_1(not_small_1_y), .in_2(A2), .in_3(not_small_3_y), .in_4(A0), .out_5(D5));
  AND4 and4_7 (.in_1(not_small_1_y), .in_2(A2), .in_3(A1), .in_4(not_small_4_y), .out_5(D6));
  AND4 and4_8 (.in_1(not_small_1_y), .in_2(A2), .in_3(A1), .in_4(A0), .out_5(D7));
  AND4 and4_9 (.in_1(A3), .in_2(not_small_2_y), .in_3(not_small_3_y), .in_4(not_small_4_y), .out_5(D8));
  AND4 and4_10 (.in_1(A3), .in_2(not_small_2_y), .in_3(not_small_3_y), .in_4(A0), .out_5(D9));
  AND4 and4_11 (.in_1(A3), .in_2(not_small_2_y), .in_3(A1), .in_4(not_small_4_y), .out_5(DA));
  AND4 and4_12 (.in_1(A3), .in_2(not_small_2_y), .in_3(A1), .in_4(A0), .out_5(DB));
  AND4 and4_13 (.in_1(A3), .in_2(A2), .in_3(not_small_3_y), .in_4(not_small_4_y), .out_5(DC));
  AND4 and4_14 (.in_1(A3), .in_2(A2), .in_3(not_small_3_y), .in_4(A0), .out_5(DD));
  AND4 and4_15 (.in_1(A3), .in_2(A2), .in_3(A1), .in_4(not_small_4_y), .out_5(DE));
  AND4 and4_16 (.in_1(A3), .in_2(A2), .in_3(A1), .in_4(A0), .out_5(DF));
endmodule

module CPU (
  input  RUN
);

  wire clock_1_out, clock_2_execute, clock_2_execute_write, clock_2_fetch, clock_2_fetch_write,
       control_unit_1_addr_mux_ir, control_unit_1_addr_mux_pc, control_unit_1_alu_add,
       control_unit_1_alu_and, control_unit_1_alu_xor, control_unit_1_halt, control_unit_1_ir_write,
       control_unit_1_memory_write, control_unit_1_pc_increment, control_unit_1_pc_load,
       control_unit_1_pc_write, control_unit_1_r_mux_alu, control_unit_1_r_mux_ir, control_unit_1_r_mux_mem,
       control_unit_1_r_mux_write, ir_1_a0, ir_1_a1, ir_1_a2, ir_1_a3, n2_way_r_mux_1_out_11,
       n2_way_r_mux_1_out_12, n2_way_r_mux_1_out_13, n2_way_r_mux_1_out_14, n3_way_r_mux_1_out_10,
       n3_way_r_mux_1_out_11, n3_way_r_mux_1_out_12, n3_way_r_mux_1_out_13, n3_way_r_mux_1_out_14,
       n3_way_r_mux_1_out_15, n3_way_r_mux_1_out_16, n3_way_r_mux_1_out_17, pc_1_o0, pc_1_o1, pc_1_o2,
       pc_1_o3;
  wire [3:1] ir_1_k1;
  wire [7:0] alu_1_out_6, n8_bit_r_1_out_11, n16_byte_memory_bank_1_out_8;

  ALU alu_1 (
    .in_4(n8_bit_r_1_out_11), .in_5(n16_byte_memory_bank_1_out_8), .out_6(alu_1_out_6),
    .OE_Adder(control_unit_1_alu_add), .OE_AND(control_unit_1_alu_and), .OE_XOR(control_unit_1_alu_xor));
  _8_bit_R u_8_bit_r_1 (
    .A0(n3_way_r_mux_1_out_17), .in_2(n3_way_r_mux_1_out_16), .in_3(n3_way_r_mux_1_out_15),
    .in_4(n3_way_r_mux_1_out_14), .in_5(n3_way_r_mux_1_out_13), .in_6(n3_way_r_mux_1_out_12),
    .in_7(n3_way_r_mux_1_out_11), .in_8(n3_way_r_mux_1_out_10), .R_WRITE(control_unit_1_r_mux_write),
    .out_11(n8_bit_r_1_out_11), .Clock(clock_1_out));
  _3_way_R_MUX u_3_way_r_mux_1 (
    .R_MUX_ALU(control_unit_1_r_mux_alu), .R_MUX_MEM(control_unit_1_r_mux_mem),
    .R_MUX_IR(control_unit_1_r_mux_ir), .ALU_Output(alu_1_out_6), .out_10(n3_way_r_mux_1_out_10),
    .out_11(n3_way_r_mux_1_out_11), .out_12(n3_way_r_mux_1_out_12), .out_13(n3_way_r_mux_1_out_13),
    .out_14(n3_way_r_mux_1_out_14), .out_15(n3_way_r_mux_1_out_15), .out_16(n3_way_r_mux_1_out_16),
    .out_17(n3_way_r_mux_1_out_17), .Memory_Output(n16_byte_memory_bank_1_out_8), .in_1(ir_1_a3),
    .in_2(ir_1_a2), .in_3(ir_1_a1), .in_4(ir_1_a0));
  IR ir_1 (
    .Write(control_unit_1_ir_write), .K3(ir_1_k1[3]), .K2(ir_1_k1[2]), .K1(ir_1_k1[1]), .A2(ir_1_a2),
    .A1(ir_1_a1), .A0(ir_1_a0), .A3(ir_1_a3), .in_1(n16_byte_memory_bank_1_out_8), .Clock(clock_1_out));
  Clock_part #(.highDuration(2), .lowDuration(2)) clock_1 (.out(clock_1_out));
  Control_Unit control_unit_1 (
    .Execute(clock_2_execute), .Execute_Write(clock_2_execute_write),
    .Memory_Write(control_unit_1_memory_write), .ALU_Add(control_unit_1_alu_add),
    .ALU_AND(control_unit_1_alu_and), .ALU_XOR(control_unit_1_alu_xor), .PC_Load(control_unit_1_pc_load),
    .PC_Increment(control_unit_1_pc_increment), .Addr_MUX_IR(control_unit_1_addr_mux_ir),
    .R_MUX_IR(control_unit_1_r_mux_ir), .IR_Write(control_unit_1_ir_write),
    .Fetch_Write(clock_2_fetch_write), .R_MUX_MEM(control_unit_1_r_mux_mem),
    .R_MUX_ALU(control_unit_1_r_mux_alu), .Fetch(clock_2_fetch), .Addr_MUX_PC(control_unit_1_addr_mux_pc),
    .R_MUX_Write(control_unit_1_r_mux_write), .in_8(n8_bit_r_1_out_11), .PC_Write(control_unit_1_pc_write),
    ._4(ir_1_k1[2]), ._8(ir_1_k1[3]), ._2(ir_1_k1[1]), .HALT(control_unit_1_halt));
  Clock clock_2 (
    .Clock(clock_1_out), .Fetch(clock_2_fetch), .Fetch_Write(clock_2_fetch_write), .Execute(clock_2_execute),
    .Execute_Write(clock_2_execute_write), .Run(RUN), .Halt(control_unit_1_halt));
  _2_way_R_MUX u_2_way_r_mux_1 (
    .Addr_MUX_PC(control_unit_1_addr_mux_pc), .Addr_MUX_IR(control_unit_1_addr_mux_ir), .L_4(ir_1_a3),
    .H_4(pc_1_o3), .L(ir_1_a2), .H(pc_1_o2), .L_2(ir_1_a1), .H_2(pc_1_o1), .L_3(ir_1_a0), .H_3(pc_1_o0),
    .out_11(n2_way_r_mux_1_out_11), .out_12(n2_way_r_mux_1_out_12), .out_13(n2_way_r_mux_1_out_13),
    .out_14(n2_way_r_mux_1_out_14));
  PC pc_1 (
    .L3(ir_1_a3), .L2(ir_1_a2), .L1(ir_1_a1), .L0(ir_1_a0), .Load(control_unit_1_pc_load),
    .Increment(control_unit_1_pc_increment), .Write(control_unit_1_pc_write), .O1(pc_1_o1), .O0(pc_1_o0),
    .O3(pc_1_o3), .Clock(clock_1_out), .O2(pc_1_o2));  // open: STEP
  _16_byte_Memory_Bank u_16_byte_memory_bank_1 (
    ._8(n2_way_r_mux_1_out_11), ._4(n2_way_r_mux_1_out_12), ._2(n2_way_r_mux_1_out_13),
    ._1(n2_way_r_mux_1_out_14), .out_8(n16_byte_memory_bank_1_out_8),
    .Memory_Write(control_unit_1_memory_write), .in_1(n8_bit_r_1_out_11), .Clock(clock_1_out));
endmodule

module UI (
  input  RUN,
  input  [3:0] Addr,
  input  [3:0] Data,
  input  [3:0] in_4,
  output out_5,
  output out_6,
  output out_7,
  output out_8,
  output out_9,
  output out_10,
  output out_11,
  output out_12
);

  wire cpu_for_interface_1_halt, Load_out, Look_out, Step_out;

  Button Load (.out(Load_out));
  Button Step (.out(Step_out));
  Button Look (.out(Look_out));
  CPU_For_Interface cpu_for_interface_1 (
    .RUN(RUN), ._8(Data[3]), ._4(Data[2]), ._2(Data[1]), ._1(Data[0]), ._8_2(in_4[3]), ._4_2(in_4[2]),
    ._2_2(in_4[1]), ._1_2(in_4[0]),
    .Memory_Output({out_5, out_6, out_7, out_8, out_9, out_10, out_11, out_12}), .Look(Look_out),
    .A3(Addr[3]), .A2(Addr[2]), .A1(Addr[1]), .A0(Addr[0]), .Read_Write_Button(Load_out),
    .HALT(cpu_for_interface_1_halt), .STEP(Step_out));
  LED HALT (.in(cpu_for_interface_1_halt));

  // Notes on the sheet:
  //   Steps:
  //   1. Enable Simulation and Enable Auto Ticks. Set tick frequency to 2 Hz ideally.
  //   Hold Load button when loading each instruction, for ideally 5 seconds at 1 Hz tick frequency.
  //   4. Once done, switch RUN pin to 1, and let the programs be executed, until HALT light becomes green.
  //   2. Leave the RUN pin at default 0. Start feeding instructions in 8-bit DATA pins to respective 4-bit ADDR address.
  //   3. Press Look at each address to ensure your instructions have been correctly loaded. Your instruction should show up at bottom-right 8-bit output
  //   Never leave the default 0000 address without any instructions, otherwise the program will HALT!
  //   When the HALT light becomes green, it means all programs have been successfully executed.
  //   After the light becomes green, turn RUN pin off, and then input your desired address and press Look.
endmodule

module CPU_For_Interface (
  input  _8,
  input  _4,
  input  _2,
  input  _1,
  input  _8_2,
  input  _4_2,
  input  _2_2,
  input  _1_2,
  input  RUN,
  input  STEP,
  input  A3,
  input  A2,
  input  A1,
  input  A0,
  input  Read_Write_Button,
  input  Look,
  output HALT,
  output [7:0] Memory_Output
);

  wire clock_1_out, clock_2_execute, clock_2_execute_write, clock_2_fetch, clock_2_fetch_write,
       control_unit_1_addr_mux_ir, control_unit_1_addr_mux_pc, control_unit_1_alu_add,
       control_unit_1_alu_and, control_unit_1_alu_xor, control_unit_1_ir_write, control_unit_1_memory_write,
       control_unit_1_pc_increment, control_unit_1_pc_load, control_unit_1_pc_write,
       control_unit_1_r_mux_alu, control_unit_1_r_mux_ir, control_unit_1_r_mux_mem,
       control_unit_1_r_mux_write, ir_1_a0, ir_1_a1, ir_1_a2, ir_1_a3, n1_bit_decider_1_out_4,
       n3_way_r_mux_1_out_10, n3_way_r_mux_1_out_11, n3_way_r_mux_1_out_12, n3_way_r_mux_1_out_13,
       n3_way_r_mux_1_out_14, n3_way_r_mux_1_out_15, n3_way_r_mux_1_out_16, n3_way_r_mux_1_out_17, not_1_out,
       pc_1_o0, pc_1_o1, pc_1_o2, pc_1_o3;
  wire [3:0] n2_way_r_mux_1_out_14, n4_bit_decider_1_out_4;
  wire [3:1] ir_1_k1;
  wire [7:0] alu_1_out_6, n8_bit_decider_1_out_4, n8_bit_r_1_out_11, n16_byte_memory_bank_1_out_8;

  ALU alu_1 (
    .in_4(n8_bit_decider_1_out_4), .in_5(n16_byte_memory_bank_1_out_8), .out_6(alu_1_out_6),
    .OE_Adder(control_unit_1_alu_add), .OE_AND(control_unit_1_alu_and), .OE_XOR(control_unit_1_alu_xor));
  _8_bit_R u_8_bit_r_1 (
    .A0(n3_way_r_mux_1_out_17), .in_2(n3_way_r_mux_1_out_16), .in_3(n3_way_r_mux_1_out_15),
    .in_4(n3_way_r_mux_1_out_14), .in_5(n3_way_r_mux_1_out_13), .in_6(n3_way_r_mux_1_out_12),
    .in_7(n3_way_r_mux_1_out_11), .in_8(n3_way_r_mux_1_out_10), .R_WRITE(control_unit_1_r_mux_write),
    .out_11(n8_bit_r_1_out_11), .Clock(clock_1_out));
  _3_way_R_MUX u_3_way_r_mux_1 (
    .R_MUX_ALU(control_unit_1_r_mux_alu), .R_MUX_MEM(control_unit_1_r_mux_mem),
    .R_MUX_IR(control_unit_1_r_mux_ir), .ALU_Output(alu_1_out_6), .out_10(n3_way_r_mux_1_out_10),
    .out_11(n3_way_r_mux_1_out_11), .out_12(n3_way_r_mux_1_out_12), .out_13(n3_way_r_mux_1_out_13),
    .out_14(n3_way_r_mux_1_out_14), .out_15(n3_way_r_mux_1_out_15), .out_16(n3_way_r_mux_1_out_16),
    .out_17(n3_way_r_mux_1_out_17), .Memory_Output(n16_byte_memory_bank_1_out_8), .in_1(ir_1_a3),
    .in_2(ir_1_a2), .in_3(ir_1_a1), .in_4(ir_1_a0));
  IR ir_1 (
    .Write(control_unit_1_ir_write), .K3(ir_1_k1[3]), .K2(ir_1_k1[2]), .K1(ir_1_k1[1]), .A2(ir_1_a2),
    .A1(ir_1_a1), .A0(ir_1_a0), .A3(ir_1_a3), .in_1(n16_byte_memory_bank_1_out_8), .Clock(clock_1_out));
  Clock_part #(.highDuration(2), .lowDuration(2)) clock_1 (.out(clock_1_out));
  _8_bit_Decider u_8_bit_decider_1 (
    .in_1(not_1_out), .in_2({_8, _4, _2, _1, _8_2, _4_2, _2_2, _1_2}), .in_3(n8_bit_r_1_out_11),
    .out_4(n8_bit_decider_1_out_4));
  Control_Unit control_unit_1 (
    .Execute(clock_2_execute), .Execute_Write(clock_2_execute_write),
    .Memory_Write(control_unit_1_memory_write), .ALU_Add(control_unit_1_alu_add),
    .ALU_AND(control_unit_1_alu_and), .ALU_XOR(control_unit_1_alu_xor), .PC_Load(control_unit_1_pc_load),
    .PC_Increment(control_unit_1_pc_increment), .Addr_MUX_IR(control_unit_1_addr_mux_ir),
    .R_MUX_IR(control_unit_1_r_mux_ir), .IR_Write(control_unit_1_ir_write),
    .Fetch_Write(clock_2_fetch_write), .R_MUX_MEM(control_unit_1_r_mux_mem),
    .R_MUX_ALU(control_unit_1_r_mux_alu), .Fetch(clock_2_fetch), .Addr_MUX_PC(control_unit_1_addr_mux_pc),
    .R_MUX_Write(control_unit_1_r_mux_write), .in_8(n8_bit_r_1_out_11), .PC_Write(control_unit_1_pc_write),
    ._4(ir_1_k1[2]), ._8(ir_1_k1[3]), ._2(ir_1_k1[1]), .HALT(HALT));
  not not_1 (not_1_out, RUN);
  Clock clock_2 (
    .Clock(clock_1_out), .Fetch(clock_2_fetch), .Fetch_Write(clock_2_fetch_write), .Execute(clock_2_execute),
    .Execute_Write(clock_2_execute_write), .Run(RUN), .Halt(HALT));
  _2_way_R_MUX u_2_way_r_mux_1 (
    .Addr_MUX_PC(control_unit_1_addr_mux_pc), .Addr_MUX_IR(control_unit_1_addr_mux_ir), .L_4(ir_1_a3),
    .H_4(pc_1_o3), .L(ir_1_a2), .H(pc_1_o2), .L_2(ir_1_a1), .H_2(pc_1_o1), .L_3(ir_1_a0), .H_3(pc_1_o0),
    .out_11(n2_way_r_mux_1_out_14[3]), .out_12(n2_way_r_mux_1_out_14[2]), .out_13(n2_way_r_mux_1_out_14[1]),
    .out_14(n2_way_r_mux_1_out_14[0]));
  _1_bit_Decider u_1_bit_decider_1 (
    .in_3(not_1_out), .in_1(Read_Write_Button), .in_2(control_unit_1_memory_write),
    .out_4(n1_bit_decider_1_out_4));
  PC pc_1 (
    .L3(ir_1_a3), .L2(ir_1_a2), .L1(ir_1_a1), .L0(ir_1_a0), .Load(control_unit_1_pc_load),
    .Increment(control_unit_1_pc_increment), .Write(control_unit_1_pc_write), .O1(pc_1_o1), .O0(pc_1_o0),
    .O3(pc_1_o3), .Clock(clock_1_out), .O2(pc_1_o2), .STEP(STEP));
  _4_bit_Decider u_4_bit_decider_1 (
    .in_3(not_1_out), .in_1({A3, A2, A1, A0}), .in_2(n2_way_r_mux_1_out_14), .out_4(n4_bit_decider_1_out_4));
  _16_byte_Memory_Bank u_16_byte_memory_bank_1 (
    ._8(n4_bit_decider_1_out_4[0]), ._4(n4_bit_decider_1_out_4[1]), ._2(n4_bit_decider_1_out_4[2]),
    ._1(n4_bit_decider_1_out_4[3]), .out_8(n16_byte_memory_bank_1_out_8),
    .Memory_Write(n1_bit_decider_1_out_4), .in_1(n8_bit_decider_1_out_4), .Clock(clock_1_out));
  _9_And u_9_and_1 (.in_2(n16_byte_memory_bank_1_out_8), .out_3(Memory_Output), .in_1(Look));

  // Notes on the sheet:
  //   A5 = 1010 0101
  //   26 = 0010 0110
  //   C7 = 1100 0111
endmodule

module PC (
  input  L3,
  input  L2,
  input  L1,
  input  L0,
  input  Load,
  input  Increment,
  input  Clock,
  input  Write,
  input  STEP,
  output O3,
  output O2,
  output O1,
  output O0
);

  wire incrementer_4bit_1_out_6, incrementer_4bit_1_out_7, incrementer_4bit_1_out_8,
       incrementer_4bit_1_out_9, n1_bit_decider_1_out_4, n2_way_bus_mux_1_out_11, n2_way_bus_mux_1_out_12,
       n2_way_bus_mux_1_out_13, n2_way_bus_mux_1_out_14;

  _1_bit_Decider u_1_bit_decider_1 (.in_3(STEP), .in_1(1'b1), .in_2(Write), .out_4(n1_bit_decider_1_out_4));
  _2_way_bus_mux u_2_way_bus_mux_1 (
    .Increment(Increment), .Load(Load), .L_4(L3), .H_4(incrementer_4bit_1_out_6), .L(L2),
    .H(incrementer_4bit_1_out_7), .L_2(L1), .H_2(incrementer_4bit_1_out_8), .L_3(L0),
    .H_3(incrementer_4bit_1_out_9), .out_11(n2_way_bus_mux_1_out_11), .out_12(n2_way_bus_mux_1_out_12),
    .out_13(n2_way_bus_mux_1_out_13), .out_14(n2_way_bus_mux_1_out_14));
  _4_bit_register u_4_bit_register_1 (
    .write(n1_bit_decider_1_out_4), .Clock(Clock), .\input (n2_way_bus_mux_1_out_11),
    .input_2(n2_way_bus_mux_1_out_12), .input_3(n2_way_bus_mux_1_out_13), .input_4(n2_way_bus_mux_1_out_14),
    .out_7(O3), .out_8(O2), .out_9(O1), .out_10(O0));
  Incrementer_4bit incrementer_4bit_1 (
    .in_1(O3), .in_2(O2), .in_3(O1), .in_4(O0), .out_6(incrementer_4bit_1_out_6),
    .out_7(incrementer_4bit_1_out_7), .out_8(incrementer_4bit_1_out_8), .out_9(incrementer_4bit_1_out_9));  // open: Overflow
endmodule

module Control_Unit (
  input  Execute,
  input  Execute_Write,
  input  Fetch,
  input  Fetch_Write,
  input  _2,
  input  _4,
  input  _8,
  input  [7:0] in_8,
  output HALT,
  output ALU_Add,
  output ALU_AND,
  output ALU_XOR,
  output Memory_Write,
  output PC_Write,
  output PC_Increment,
  output PC_Load,
  output R_MUX_ALU,
  output R_MUX_MEM,
  output Addr_MUX_PC,
  output R_MUX_IR,
  output Addr_MUX_IR,
  output R_MUX_Write,
  output IR_Write
);

  wire n4_nor_7_out_5, n4_nor_8_out_5, n4_nor_10_out_5, n4_nor_11_out_5, n4_nor_12_out_5, n4_nor_13_out_5,
       n4_nor_14_out_5, not_small_1_y, not_small_2_y, not_small_3_y, not_small_4_y, not_small_5_y,
       not_small_6_y, not_small_7_y, not_small_8_y, notgate_1_y, notgate_2_y, notgate_3_y, notgate_4_y,
       notgate_5_y, notgate_6_y, notgate_7_y, notgate_8_y, notgate_9_y, notgate_10_y, notgate_11_y,
       notgate_12_y, notgate_13_y, notgate_14_y, notgate_15_y, notgate_16_y, notgate_17_y, notgate_18_y,
       notgate_19_y, notgate_20_y, notgate_22_y, notgate_23_y, notgate_24_y, notgate_25_y, notgate_26_y,
       notgate_27_y, notgate_28_y, notgate_29_y, notgate_30_y, notgate_31_y, notgate_32_y, notgate_33_y,
       notgate_34_y, notgate_35_y, notgate_36_y, notgate_37_y, notgate_38_y, notgate_39_y, notgate_40_y,
       notgate_41_y;

  OR3 or3_1 (.in_1(ALU_XOR), .in_2(ALU_AND), .in_3(ALU_Add), .out_4(R_MUX_ALU));
  NOTGate notgate_1 (.Y(notgate_1_y), .X(_4));
  NOTGate notgate_2 (.Y(notgate_2_y), .X(_4));
  NOTGate notgate_3 (.Y(notgate_3_y), .X(_8));
  NOTGate notgate_4 (.Y(notgate_4_y), .X(_8));
  NOTGate notgate_5 (.Y(notgate_5_y), .X(_8));
  NOTGate notgate_6 (.Y(notgate_6_y), .X(_8));
  NOTGate notgate_7 (.Y(notgate_7_y), .X(Execute));
  _4_nor u_4_nor_1 (.in_1(notgate_7_y), .in_2(_2), .in_3(_4), .in_4(_8), .out_5(HALT));
  NOTGate notgate_8 (.Y(notgate_8_y), .X(_2));
  NOTGate notgate_9 (.Y(notgate_9_y), .X(Execute));
  _4_nor u_4_nor_2 (.in_1(notgate_9_y), .in_2(notgate_8_y), .in_3(_4), .in_4(_8), .out_5(ALU_Add));
  NOTGate notgate_10 (.Y(notgate_10_y), .X(Execute));
  _4_nor u_4_nor_3 (.in_1(notgate_10_y), .in_2(_2), .in_3(notgate_1_y), .in_4(_8), .out_5(ALU_AND));
  NOTGate notgate_11 (.Y(notgate_11_y), .X(Execute));
  NOTGate notgate_12 (.Y(notgate_12_y), .X(_2));
  _4_nor u_4_nor_4 (.in_1(notgate_11_y), .in_2(notgate_12_y), .in_3(notgate_2_y), .in_4(_8), .out_5(ALU_XOR));
  NOTGate notgate_13 (.Y(notgate_13_y), .X(Execute));
  _4_nor u_4_nor_5 (.in_1(notgate_13_y), .in_2(_2), .in_3(_4), .in_4(notgate_3_y), .out_5(R_MUX_IR));
  NOTGate notgate_14 (.Y(notgate_14_y), .X(Execute));
  NOTGate notgate_15 (.Y(notgate_15_y), .X(_2));
  _4_nor u_4_nor_6 (.in_1(notgate_14_y), .in_2(notgate_15_y), .in_3(_4), .in_4(notgate_4_y), .out_5(R_MUX_MEM));
  NOTGate notgate_16 (.Y(notgate_16_y), .X(Execute));
  NOTGate notgate_17 (.Y(notgate_17_y), .X(_4));
  _4_nor u_4_nor_7 (.in_1(notgate_16_y), .in_2(_2), .in_3(notgate_17_y), .in_4(notgate_5_y), .out_5(n4_nor_7_out_5));
  NOTGate notgate_18 (.Y(notgate_18_y), .X(_2));
  NOTGate notgate_19 (.Y(notgate_19_y), .X(_4));
  _4_nor u_4_nor_8 (
    .in_1(notgate_20_y), .in_2(notgate_18_y), .in_3(notgate_19_y), .in_4(notgate_6_y), .out_5(n4_nor_8_out_5));
  NOT_Small not_small_1 (.Y(not_small_1_y), .X(in_8[4]));
  NOT_Small not_small_2 (.Y(not_small_2_y), .X(in_8[6]));
  NOT_Small not_small_3 (.Y(not_small_3_y), .X(in_8[0]));
  NOT_Small not_small_4 (.Y(not_small_4_y), .X(in_8[5]));
  NOT_Small not_small_5 (.Y(not_small_5_y), .X(in_8[2]));
  NOT_Small not_small_6 (.Y(not_small_6_y), .X(in_8[7]));
  NOT_Small not_small_7 (.Y(not_small_7_y), .X(in_8[1]));
  NOT_Small not_small_8 (.Y(not_small_8_y), .X(in_8[3]));
  and and_1 (PC_Load, not_small_6_y, not_small_2_y, not_small_4_y, not_small_1_y, not_small_8_y, not_small_5_y, not_small_7_y, not_small_3_y, n4_nor_8_out_5);
  NOTGate notgate_20 (.Y(notgate_20_y), .X(Execute));
  NOTGate notgate_21 (.Y(PC_Increment), .X(PC_Load));
  OR3 or3_2 (.in_1(R_MUX_ALU), .in_2(n4_nor_7_out_5), .in_3(R_MUX_MEM), .out_4(Addr_MUX_IR));
  NOTGate notgate_22 (.Y(notgate_22_y), .X(_2));
  NOTGate notgate_23 (.Y(notgate_23_y), .X(_4));
  NOTGate notgate_24 (.Y(notgate_24_y), .X(_2));
  NOTGate notgate_25 (.Y(notgate_25_y), .X(_4));
  NOTGate notgate_26 (.Y(notgate_26_y), .X(_8));
  NOTGate notgate_27 (.Y(notgate_27_y), .X(_8));
  NOTGate notgate_28 (.Y(notgate_28_y), .X(_8));
  NOTGate notgate_29 (.Y(notgate_29_y), .X(_8));
  NOTGate notgate_30 (.Y(notgate_30_y), .X(Execute_Write));
  _4_nor u_4_nor_9 (.in_1(notgate_30_y), .in_2(_2), .in_3(_4), .in_4(_8));  // open: out_5
  NOTGate notgate_31 (.Y(notgate_31_y), .X(Execute_Write));
  _4_nor u_4_nor_10 (.in_1(notgate_31_y), .in_2(notgate_22_y), .in_3(_4), .in_4(_8), .out_5(n4_nor_10_out_5));
  NOTGate notgate_32 (.Y(notgate_32_y), .X(Execute_Write));
  _4_nor u_4_nor_11 (.in_1(notgate_32_y), .in_2(_2), .in_3(notgate_23_y), .in_4(_8), .out_5(n4_nor_11_out_5));
  NOTGate notgate_33 (.Y(notgate_33_y), .X(Execute_Write));
  _4_nor u_4_nor_12 (.in_1(notgate_33_y), .in_2(notgate_24_y), .in_3(notgate_25_y), .in_4(_8), .out_5(n4_nor_12_out_5));
  NOTGate notgate_34 (.Y(notgate_34_y), .X(Execute_Write));
  _4_nor u_4_nor_13 (.in_1(notgate_34_y), .in_2(_2), .in_3(_4), .in_4(notgate_26_y), .out_5(n4_nor_13_out_5));
  NOTGate notgate_35 (.Y(notgate_35_y), .X(Execute_Write));
  NOTGate notgate_36 (.Y(notgate_36_y), .X(_2));
  _4_nor u_4_nor_14 (.in_1(notgate_35_y), .in_2(notgate_36_y), .in_3(_4), .in_4(notgate_27_y), .out_5(n4_nor_14_out_5));
  NOTGate notgate_37 (.Y(notgate_37_y), .X(Execute_Write));
  NOTGate notgate_38 (.Y(notgate_38_y), .X(_4));
  _4_nor u_4_nor_15 (.in_1(notgate_37_y), .in_2(_2), .in_3(notgate_38_y), .in_4(notgate_28_y), .out_5(Memory_Write));
  NOTGate notgate_39 (.Y(notgate_39_y), .X(_2));
  NOTGate notgate_40 (.Y(notgate_40_y), .X(_4));
  _4_nor u_4_nor_16 (
    .in_1(notgate_41_y), .in_2(notgate_39_y), .in_3(notgate_40_y), .in_4(notgate_29_y));  // open: out_5
  _5OR u_5or_1 (
    .in_1(n4_nor_10_out_5), .in_2(n4_nor_11_out_5), .in_3(n4_nor_12_out_5), .in_4(n4_nor_13_out_5),
    .in_5(n4_nor_14_out_5), .out_6(R_MUX_Write));
  NOTGate notgate_41 (.Y(notgate_41_y), .X(Execute_Write));

  assign Addr_MUX_PC = Fetch;
  assign IR_Write = Fetch_Write;
  assign PC_Write = Execute_Write;
endmodule

module ALU (
  input  OE_Adder,
  input  OE_AND,
  input  OE_XOR,
  input  [7:0] in_4,
  input  [7:0] in_5,
  output [7:0] out_6
);

  wire decoder_1_d1, decoder_1_d2, decoder_1_d4;
  wire [7:0] eightbitadder_using_maj_odd_1_sum, n8_bit_and_1_out_3, n8_bit_xor_1_out_3, n9_and_1_out_3,
       n9_and_2_out_3, n9_and_3_out_3;

  Pull_Resistor pull_resistor_1 (.node(in_4));
  EightbitAdder_Using_MAJ___ODD eightbitadder_using_maj_odd_1 (
    .A(in_4), .B(in_5), .Sum(eightbitadder_using_maj_odd_1_sum), .Carry_in(1'b0));  // open: Carry_out
  _8_bit_AND u_8_bit_and_1 (.in_1(in_4), .in_2(in_5), .out_3(n8_bit_and_1_out_3));
  _8_bit_XOR u_8_bit_xor_1 (.in_1(in_4), .in_2(in_5), .out_3(n8_bit_xor_1_out_3));
  Decoder decoder_1 (
    .A(OE_XOR), .B(OE_AND), .C(OE_Adder), .D4(decoder_1_d4), .D2(decoder_1_d2), .D1(decoder_1_d1));  // open: D7, D6, D5, D3, D0
  _9_And u_9_and_1 (.in_2(eightbitadder_using_maj_odd_1_sum), .out_3(n9_and_1_out_3), .in_1(decoder_1_d1));
  _9_And u_9_and_2 (.in_2(n8_bit_and_1_out_3), .out_3(n9_and_2_out_3), .in_1(decoder_1_d2));
  _9_And u_9_and_3 (.in_2(n8_bit_xor_1_out_3), .out_3(n9_and_3_out_3), .in_1(decoder_1_d4));
  OR or_1 (.in_2(n9_and_2_out_3), .out_4(out_6), .in_1(n9_and_1_out_3), .in_3(n9_and_3_out_3));
endmodule

module _2_way_R_MUX (
  input  H,
  input  H_2,
  input  H_3,
  input  H_4,
  input  L,
  input  L_2,
  input  L_3,
  input  L_4,
  input  Addr_MUX_PC,
  input  Addr_MUX_IR,
  output out_11,
  output out_12,
  output out_13,
  output out_14
);

  wire and_gate_1_out_3, and_gate_2_out_3, and_gate_3_out_3, and_gate_4_out_3, and_gate_5_out_3,
       and_gate_6_out_3, and_gate_7_out_3, and_gate_8_out_3;

  AND_Gate and_gate_1 (.in_1(Addr_MUX_PC), .in_2(H_4), .out_3(and_gate_1_out_3));
  AND_Gate and_gate_2 (.in_1(Addr_MUX_IR), .in_2(L_4), .out_3(and_gate_2_out_3));
  OR_Gate or_gate_1 (.in_1(and_gate_1_out_3), .in_2(and_gate_2_out_3), .out_3(out_11));
  AND_Gate and_gate_3 (.in_1(Addr_MUX_PC), .in_2(H), .out_3(and_gate_3_out_3));
  AND_Gate and_gate_4 (.in_1(Addr_MUX_IR), .in_2(L), .out_3(and_gate_4_out_3));
  OR_Gate or_gate_2 (.in_1(and_gate_3_out_3), .in_2(and_gate_4_out_3), .out_3(out_12));
  AND_Gate and_gate_5 (.in_1(Addr_MUX_PC), .in_2(H_2), .out_3(and_gate_5_out_3));
  AND_Gate and_gate_6 (.in_1(Addr_MUX_IR), .in_2(L_2), .out_3(and_gate_6_out_3));
  OR_Gate or_gate_3 (.in_1(and_gate_5_out_3), .in_2(and_gate_6_out_3), .out_3(out_13));
  AND_Gate and_gate_7 (.in_1(Addr_MUX_PC), .in_2(H_3), .out_3(and_gate_7_out_3));
  AND_Gate and_gate_8 (.in_1(Addr_MUX_IR), .in_2(L_3), .out_3(and_gate_8_out_3));
  OR_Gate or_gate_4 (.in_1(and_gate_7_out_3), .in_2(and_gate_8_out_3), .out_3(out_14));
endmodule

module Clock (
  input  Run,
  input  Clock,
  input  Halt,
  output Fetch,
  output Fetch_Write,
  output Execute,
  output Execute_Write
);

  wire and_gate_3_out_3, and_gate_for_clock_1_out_3;

  AND_Gate and_gate_1 (.in_1(and_gate_3_out_3), .in_2(Fetch), .out_3(Fetch_Write));
  NOTGate notgate_1 (.Y(Fetch), .X(Execute));
  AND_Gate and_gate_2 (.in_1(and_gate_3_out_3), .in_2(Execute), .out_3(Execute_Write));
  D_Flip_Flop #(.trigger("falling")) d_ff_1 (
    .clk(and_gate_3_out_3), .D(Fetch), .Q(Execute));  // open: Qn, preset, en, reset
  Clock_part clock_1 ();  // open: out
  AND_gate_for_clock and_gate_for_clock_1 (.in_1(Run), .in_2(Halt), .out_3(and_gate_for_clock_1_out_3));
  AND_Gate and_gate_3 (.in_1(Clock), .in_2(and_gate_for_clock_1_out_3), .out_3(and_gate_3_out_3));
endmodule

module _3_way_R_MUX (
  input  in_1,
  input  in_2,
  input  in_3,
  input  in_4,
  input  [7:0] Memory_Output,
  input  [7:0] ALU_Output,
  input  R_MUX_ALU,
  input  R_MUX_MEM,
  input  R_MUX_IR,
  output out_10,
  output out_11,
  output out_12,
  output out_13,
  output out_14,
  output out_15,
  output out_16,
  output out_17
);

  wire and_gate_1_out_3, and_gate_2_out_3, and_gate_3_out_3, and_gate_4_out_3, and_gate_5_out_3,
       and_gate_6_out_3, and_gate_7_out_3, and_gate_8_out_3, and_gate_9_out_3, and_gate_10_out_3,
       and_gate_11_out_3, and_gate_12_out_3, and_gate_13_out_3, and_gate_14_out_3, and_gate_15_out_3,
       and_gate_16_out_3, and_gate_17_out_3, and_gate_18_out_3, and_gate_19_out_3, and_gate_20_out_3,
       and_gate_21_out_3, and_gate_22_out_3, and_gate_23_out_3, and_gate_24_out_3;

  AND_Gate and_gate_1 (.in_1(R_MUX_ALU), .in_2(ALU_Output[7]), .out_3(and_gate_1_out_3));
  AND_Gate and_gate_2 (.in_1(R_MUX_MEM), .in_2(Memory_Output[7]), .out_3(and_gate_2_out_3));
  AND_Gate and_gate_3 (.in_1(1'b0), .in_2(R_MUX_IR), .out_3(and_gate_3_out_3));
  OR3 or3_1 (.in_1(and_gate_2_out_3), .in_2(and_gate_3_out_3), .in_3(and_gate_1_out_3), .out_4(out_10));
  AND_Gate and_gate_4 (.in_1(R_MUX_ALU), .in_2(ALU_Output[6]), .out_3(and_gate_4_out_3));
  AND_Gate and_gate_5 (.in_1(R_MUX_MEM), .in_2(Memory_Output[6]), .out_3(and_gate_5_out_3));
  AND_Gate and_gate_6 (.in_1(1'b0), .in_2(R_MUX_IR), .out_3(and_gate_6_out_3));
  OR3 or3_2 (.in_1(and_gate_5_out_3), .in_2(and_gate_6_out_3), .in_3(and_gate_4_out_3), .out_4(out_11));
  AND_Gate and_gate_7 (.in_1(R_MUX_ALU), .in_2(ALU_Output[5]), .out_3(and_gate_7_out_3));
  AND_Gate and_gate_8 (.in_1(R_MUX_MEM), .in_2(Memory_Output[5]), .out_3(and_gate_8_out_3));
  AND_Gate and_gate_9 (.in_1(1'b0), .in_2(R_MUX_IR), .out_3(and_gate_9_out_3));
  OR3 or3_3 (.in_1(and_gate_8_out_3), .in_2(and_gate_9_out_3), .in_3(and_gate_7_out_3), .out_4(out_12));
  AND_Gate and_gate_10 (.in_1(R_MUX_ALU), .in_2(ALU_Output[4]), .out_3(and_gate_10_out_3));
  AND_Gate and_gate_11 (.in_1(R_MUX_MEM), .in_2(Memory_Output[4]), .out_3(and_gate_11_out_3));
  AND_Gate and_gate_12 (.in_1(1'b0), .in_2(R_MUX_IR), .out_3(and_gate_12_out_3));
  OR3 or3_4 (.in_1(and_gate_11_out_3), .in_2(and_gate_12_out_3), .in_3(and_gate_10_out_3), .out_4(out_13));
  AND_Gate and_gate_13 (.in_1(R_MUX_ALU), .in_2(ALU_Output[3]), .out_3(and_gate_13_out_3));
  AND_Gate and_gate_14 (.in_1(R_MUX_MEM), .in_2(Memory_Output[3]), .out_3(and_gate_14_out_3));
  AND_Gate and_gate_15 (.in_1(in_1), .in_2(R_MUX_IR), .out_3(and_gate_15_out_3));
  OR3 or3_5 (.in_1(and_gate_14_out_3), .in_2(and_gate_15_out_3), .in_3(and_gate_13_out_3), .out_4(out_14));
  AND_Gate and_gate_16 (.in_1(R_MUX_ALU), .in_2(ALU_Output[2]), .out_3(and_gate_16_out_3));
  AND_Gate and_gate_17 (.in_1(R_MUX_MEM), .in_2(Memory_Output[2]), .out_3(and_gate_17_out_3));
  AND_Gate and_gate_18 (.in_1(in_2), .in_2(R_MUX_IR), .out_3(and_gate_18_out_3));
  OR3 or3_6 (.in_1(and_gate_17_out_3), .in_2(and_gate_18_out_3), .in_3(and_gate_16_out_3), .out_4(out_15));
  AND_Gate and_gate_19 (.in_1(R_MUX_ALU), .in_2(ALU_Output[1]), .out_3(and_gate_19_out_3));
  AND_Gate and_gate_20 (.in_1(R_MUX_MEM), .in_2(Memory_Output[1]), .out_3(and_gate_20_out_3));
  AND_Gate and_gate_21 (.in_1(in_3), .in_2(R_MUX_IR), .out_3(and_gate_21_out_3));
  OR3 or3_7 (.in_1(and_gate_20_out_3), .in_2(and_gate_21_out_3), .in_3(and_gate_19_out_3), .out_4(out_16));
  AND_Gate and_gate_22 (.in_1(R_MUX_ALU), .in_2(ALU_Output[0]), .out_3(and_gate_22_out_3));
  AND_Gate and_gate_23 (.in_1(R_MUX_MEM), .in_2(Memory_Output[0]), .out_3(and_gate_23_out_3));
  AND_Gate and_gate_24 (.in_1(in_4), .in_2(R_MUX_IR), .out_3(and_gate_24_out_3));
  OR3 or3_8 (.in_1(and_gate_23_out_3), .in_2(and_gate_24_out_3), .in_3(and_gate_22_out_3), .out_4(out_17));
endmodule

module _8_bit_R (
  input  A0,
  input  in_2,
  input  in_3,
  input  in_4,
  input  in_5,
  input  in_6,
  input  in_7,
  input  in_8,
  input  R_WRITE,
  input  Clock,
  output [7:0] out_11
);

  _1bit_mem_CORRECT u_1bit_mem_correct_1 (.Data(A0), .Read_Write(R_WRITE), .out_3(out_11[0]));
  _1bit_mem_CORRECT u_1bit_mem_correct_2 (.Data(in_2), .Read_Write(R_WRITE), .out_3(out_11[1]));
  _1bit_mem_CORRECT u_1bit_mem_correct_3 (.Data(in_3), .Read_Write(R_WRITE), .out_3(out_11[2]));
  _1bit_mem_CORRECT u_1bit_mem_correct_4 (.Data(in_4), .Read_Write(R_WRITE), .out_3(out_11[3]));
  _1bit_mem_CORRECT u_1bit_mem_correct_5 (.Data(in_5), .Read_Write(R_WRITE), .out_3(out_11[4]));
  _1bit_mem_CORRECT u_1bit_mem_correct_6 (.Data(in_6), .Read_Write(R_WRITE), .out_3(out_11[5]));
  _1bit_mem_CORRECT u_1bit_mem_correct_7 (.Data(in_7), .Read_Write(R_WRITE), .out_3(out_11[6]));
  _1bit_mem_CORRECT u_1bit_mem_correct_8 (.Data(in_8), .Read_Write(R_WRITE), .out_3(out_11[7]));
endmodule

module IR (
  input  [7:0] in_1,
  input  Clock,
  input  Write,
  output K3,
  output K2,
  output K1,
  output A3,
  output A2,
  output A1,
  output A0
);

  wire n1bit_mem_correct_4_out_3;

  _1bit_mem_CORRECT u_1bit_mem_correct_1 (.Data(in_1[7]), .Read_Write(Write), .out_3(K3));
  _1bit_mem_CORRECT u_1bit_mem_correct_2 (.Data(in_1[6]), .Read_Write(Write), .out_3(K2));
  _1bit_mem_CORRECT u_1bit_mem_correct_3 (.Data(in_1[5]), .Read_Write(Write), .out_3(K1));
  _1bit_mem_CORRECT u_1bit_mem_correct_4 (.Data(in_1[4]), .Read_Write(Write), .out_3(n1bit_mem_correct_4_out_3));
  _1bit_mem_CORRECT u_1bit_mem_correct_5 (.Data(in_1[3]), .Read_Write(Write), .out_3(A3));
  _1bit_mem_CORRECT u_1bit_mem_correct_6 (.Data(in_1[2]), .Read_Write(Write), .out_3(A2));
  _1bit_mem_CORRECT u_1bit_mem_correct_7 (.Data(in_1[1]), .Read_Write(Write), .out_3(A1));
  _1bit_mem_CORRECT u_1bit_mem_correct_8 (.Data(in_1[0]), .Read_Write(Write), .out_3(A0));

  // Notes on the sheet:
  //   Address
  //   Opcode
endmodule

module _16_byte_Memory_Bank (
  input  [7:0] in_1,
  input  Clock,
  input  Memory_Write,
  input  _8,
  input  _4,
  input  _2,
  input  _1,
  output [7:0] out_8
);

  wire dd_4_to_32_1_out_6, dd_4_to_32_1_out_7, dd_4_to_32_1_out_8, dd_4_to_32_1_out_9, dd_4_to_32_1_out_10,
       dd_4_to_32_1_out_11, dd_4_to_32_1_out_12, dd_4_to_32_1_out_13, dd_4_to_32_1_out_14,
       dd_4_to_32_1_out_15, dd_4_to_32_1_out_16, dd_4_to_32_1_out_17, dd_4_to_32_1_out_18,
       dd_4_to_32_1_out_19, dd_4_to_32_1_out_20, dd_4_to_32_1_out_21, dd_4_to_32_1_out_22,
       dd_4_to_32_1_out_23, dd_4_to_32_1_out_24, dd_4_to_32_1_out_25, dd_4_to_32_1_out_26,
       dd_4_to_32_1_out_27, dd_4_to_32_1_out_28, dd_4_to_32_1_out_29, dd_4_to_32_1_out_30,
       dd_4_to_32_1_out_31, dd_4_to_32_1_out_32, dd_4_to_32_1_out_33, dd_4_to_32_1_out_34,
       dd_4_to_32_1_out_35, dd_4_to_32_1_out_36, dd_4_to_32_1_out_37;
  wire [7:0] n8_bit_memory_1_output, n8_bit_memory_2_output, n8_bit_memory_3_output, n8_bit_memory_4_output,
       n8_bit_memory_5_output, n8_bit_memory_6_output, n8_bit_memory_7_output, n8_bit_memory_8_output,
       n8_bit_memory_9_output, n8_bit_memory_10_output, n8_bit_memory_11_output, n8_bit_memory_12_output,
       n8_bit_memory_13_output, n8_bit_memory_14_output, n8_bit_memory_15_output, n8_bit_memory_16_output,
       n9_and_1_out_3, n9_and_2_out_3, n9_and_3_out_3, n9_and_4_out_3, n9_and_5_out_3, n9_and_6_out_3,
       n9_and_7_out_3, n9_and_8_out_3, n9_and_9_out_3, n9_and_10_out_3, n9_and_11_out_3, n9_and_12_out_3,
       n9_and_13_out_3, n9_and_14_out_3, n9_and_15_out_3, n9_and_16_out_3;

  DD_4_to_32 dd_4_to_32_1 (
    .A3(_8), .A2(_4), .A1(_2), .A0(_1), .out_6(dd_4_to_32_1_out_6), .out_7(dd_4_to_32_1_out_7),
    .out_8(dd_4_to_32_1_out_8), .out_9(dd_4_to_32_1_out_9), .out_10(dd_4_to_32_1_out_10),
    .out_11(dd_4_to_32_1_out_11), .out_12(dd_4_to_32_1_out_12), .out_13(dd_4_to_32_1_out_13),
    .out_14(dd_4_to_32_1_out_14), .out_15(dd_4_to_32_1_out_15), .out_16(dd_4_to_32_1_out_16),
    .out_17(dd_4_to_32_1_out_17), .out_18(dd_4_to_32_1_out_18), .out_19(dd_4_to_32_1_out_19),
    .out_20(dd_4_to_32_1_out_20), .out_21(dd_4_to_32_1_out_21), .out_22(dd_4_to_32_1_out_22),
    .out_23(dd_4_to_32_1_out_23), .out_24(dd_4_to_32_1_out_24), .out_25(dd_4_to_32_1_out_25),
    .out_26(dd_4_to_32_1_out_26), .out_27(dd_4_to_32_1_out_27), .out_28(dd_4_to_32_1_out_28),
    .out_29(dd_4_to_32_1_out_29), .out_30(dd_4_to_32_1_out_30), .out_31(dd_4_to_32_1_out_31),
    .out_32(dd_4_to_32_1_out_32), .out_33(dd_4_to_32_1_out_33), .out_34(dd_4_to_32_1_out_34),
    .out_35(dd_4_to_32_1_out_35), .out_36(dd_4_to_32_1_out_36), .out_37(dd_4_to_32_1_out_37), .X(Memory_Write));
  Pull_Resistor pull_resistor_1 (.node(in_1));
  _8_bit_Memory u_8_bit_memory_1 (
    .Input(in_1), .Output(n8_bit_memory_1_output), .Write(dd_4_to_32_1_out_6), .Clock(Clock));
  _8_bit_Memory u_8_bit_memory_2 (
    .Input(in_1), .Output(n8_bit_memory_2_output), .Write(dd_4_to_32_1_out_8), .Clock(Clock));
  _8_bit_Memory u_8_bit_memory_3 (
    .Input(in_1), .Output(n8_bit_memory_3_output), .Write(dd_4_to_32_1_out_10), .Clock(Clock));
  _8_bit_Memory u_8_bit_memory_4 (
    .Input(in_1), .Output(n8_bit_memory_4_output), .Write(dd_4_to_32_1_out_12), .Clock(Clock));
  _8_bit_Memory u_8_bit_memory_5 (
    .Input(in_1), .Output(n8_bit_memory_5_output), .Write(dd_4_to_32_1_out_14), .Clock(Clock));
  _8_bit_Memory u_8_bit_memory_6 (
    .Input(in_1), .Output(n8_bit_memory_6_output), .Write(dd_4_to_32_1_out_16), .Clock(Clock));
  _8_bit_Memory u_8_bit_memory_7 (
    .Input(in_1), .Output(n8_bit_memory_7_output), .Write(dd_4_to_32_1_out_18), .Clock(Clock));
  _8_bit_Memory u_8_bit_memory_8 (
    .Input(in_1), .Output(n8_bit_memory_8_output), .Write(dd_4_to_32_1_out_20), .Clock(Clock));
  _8_bit_Memory u_8_bit_memory_9 (
    .Input(in_1), .Output(n8_bit_memory_9_output), .Write(dd_4_to_32_1_out_22), .Clock(Clock));
  _8_bit_Memory u_8_bit_memory_10 (
    .Input(in_1), .Output(n8_bit_memory_10_output), .Write(dd_4_to_32_1_out_24), .Clock(Clock));
  _8_bit_Memory u_8_bit_memory_11 (
    .Input(in_1), .Output(n8_bit_memory_11_output), .Write(dd_4_to_32_1_out_26), .Clock(Clock));
  _8_bit_Memory u_8_bit_memory_12 (
    .Input(in_1), .Output(n8_bit_memory_12_output), .Write(dd_4_to_32_1_out_28), .Clock(Clock));
  _8_bit_Memory u_8_bit_memory_13 (
    .Input(in_1), .Output(n8_bit_memory_13_output), .Write(dd_4_to_32_1_out_30), .Clock(Clock));
  _8_bit_Memory u_8_bit_memory_14 (
    .Input(in_1), .Output(n8_bit_memory_14_output), .Write(dd_4_to_32_1_out_32), .Clock(Clock));
  _8_bit_Memory u_8_bit_memory_15 (
    .Input(in_1), .Output(n8_bit_memory_15_output), .Write(dd_4_to_32_1_out_34), .Clock(Clock));
  _8_bit_Memory u_8_bit_memory_16 (
    .Input(in_1), .Output(n8_bit_memory_16_output), .Write(dd_4_to_32_1_out_36), .Clock(Clock));
  _9_And u_9_and_1 (.in_2(n8_bit_memory_1_output), .out_3(n9_and_1_out_3), .in_1(dd_4_to_32_1_out_7));
  _9_And u_9_and_2 (.in_2(n8_bit_memory_2_output), .out_3(n9_and_2_out_3), .in_1(dd_4_to_32_1_out_9));
  _9_And u_9_and_3 (.in_2(n8_bit_memory_3_output), .out_3(n9_and_3_out_3), .in_1(dd_4_to_32_1_out_11));
  _9_And u_9_and_4 (.in_2(n8_bit_memory_4_output), .out_3(n9_and_4_out_3), .in_1(dd_4_to_32_1_out_13));
  _9_And u_9_and_5 (.in_2(n8_bit_memory_5_output), .out_3(n9_and_5_out_3), .in_1(dd_4_to_32_1_out_15));
  _9_And u_9_and_6 (.in_2(n8_bit_memory_6_output), .out_3(n9_and_6_out_3), .in_1(dd_4_to_32_1_out_17));
  _9_And u_9_and_7 (.in_2(n8_bit_memory_7_output), .out_3(n9_and_7_out_3), .in_1(dd_4_to_32_1_out_19));
  _9_And u_9_and_8 (.in_2(n8_bit_memory_8_output), .out_3(n9_and_8_out_3), .in_1(dd_4_to_32_1_out_21));
  _9_And u_9_and_9 (.in_2(n8_bit_memory_9_output), .out_3(n9_and_9_out_3), .in_1(dd_4_to_32_1_out_23));
  _9_And u_9_and_10 (.in_2(n8_bit_memory_10_output), .out_3(n9_and_10_out_3), .in_1(dd_4_to_32_1_out_25));
  _9_And u_9_and_11 (.in_2(n8_bit_memory_11_output), .out_3(n9_and_11_out_3), .in_1(dd_4_to_32_1_out_27));
  _9_And u_9_and_12 (.in_2(n8_bit_memory_12_output), .out_3(n9_and_12_out_3), .in_1(dd_4_to_32_1_out_29));
  _9_And u_9_and_13 (.in_2(n8_bit_memory_13_output), .out_3(n9_and_13_out_3), .in_1(dd_4_to_32_1_out_31));
  _9_And u_9_and_14 (.in_2(n8_bit_memory_14_output), .out_3(n9_and_14_out_3), .in_1(dd_4_to_32_1_out_33));
  _9_And u_9_and_15 (.in_2(n8_bit_memory_15_output), .out_3(n9_and_15_out_3), .in_1(dd_4_to_32_1_out_35));
  _9_And u_9_and_16 (.in_2(n8_bit_memory_16_output), .out_3(n9_and_16_out_3), .in_1(dd_4_to_32_1_out_37));
  _16OR u_16or_1 (
    .in_1(n9_and_1_out_3), .in_2(n9_and_2_out_3), .in_3(n9_and_3_out_3), .in_4(n9_and_4_out_3),
    .in_5(n9_and_5_out_3), .in_6(n9_and_6_out_3), .in_7(n9_and_7_out_3), .in_8(n9_and_8_out_3),
    .in_9(n9_and_9_out_3), .in_10(n9_and_10_out_3), .in_11(n9_and_11_out_3), .in_12(n9_and_12_out_3),
    .in_13(n9_and_13_out_3), .in_14(n9_and_14_out_3), .in_15(n9_and_15_out_3), .in_16(n9_and_16_out_3),
    .out_17(out_8));
endmodule

module _8_bit_Memory (
  input  [7:0] Input,
  input  Clock,
  input  Write,
  output [7:0] Output
);

  Pull_Resistor pull_resistor_1 (.node(Write));
  _1bit_mem_CORRECT u_1bit_mem_correct_1 (.Data(Input[0]), .Read_Write(Write), .out_3(Output[0]));
  _1bit_mem_CORRECT u_1bit_mem_correct_2 (.Data(Input[1]), .Read_Write(Write), .out_3(Output[1]));
  _1bit_mem_CORRECT u_1bit_mem_correct_3 (.Data(Input[2]), .Read_Write(Write), .out_3(Output[2]));
  _1bit_mem_CORRECT u_1bit_mem_correct_4 (.Data(Input[3]), .Read_Write(Write), .out_3(Output[3]));
  _1bit_mem_CORRECT u_1bit_mem_correct_5 (.Data(Input[4]), .Read_Write(Write), .out_3(Output[4]));
  _1bit_mem_CORRECT u_1bit_mem_correct_6 (.Data(Input[5]), .Read_Write(Write), .out_3(Output[5]));
  _1bit_mem_CORRECT u_1bit_mem_correct_7 (.Data(Input[6]), .Read_Write(Write), .out_3(Output[6]));
  _1bit_mem_CORRECT u_1bit_mem_correct_8 (.Data(Input[7]), .Read_Write(Write), .out_3(Output[7]));
endmodule

// REG
module _4_bit_register (
  input  \input ,
  input  input_2,
  input  input_3,
  input  input_4,
  input  write,
  input  Clock,
  output out_7,
  output out_8,
  output out_9,
  output out_10
);

  _1bit_mem_CORRECT u_1bit_mem_correct_1 (.Data(\input ), .Read_Write(write), .out_3(out_7));
  _1bit_mem_CORRECT u_1bit_mem_correct_2 (.Data(input_2), .Read_Write(write), .out_3(out_8));
  _1bit_mem_CORRECT u_1bit_mem_correct_3 (.Data(input_3), .Read_Write(write), .out_3(out_9));
  _1bit_mem_CORRECT u_1bit_mem_correct_4 (.Data(input_4), .Read_Write(write), .out_3(out_10));
endmodule

// BUS MUX
module _2_way_bus_mux (
  input  H,
  input  H_2,
  input  H_3,
  input  H_4,
  input  L,
  input  L_2,
  input  L_3,
  input  L_4,
  input  Increment,
  input  Load,
  output out_11,
  output out_12,
  output out_13,
  output out_14
);

  wire and_gate_1_out_3, and_gate_2_out_3, and_gate_3_out_3, and_gate_4_out_3, and_gate_5_out_3,
       and_gate_6_out_3, and_gate_7_out_3, and_gate_8_out_3;

  AND_Gate and_gate_1 (.in_1(Increment), .in_2(H_4), .out_3(and_gate_1_out_3));
  AND_Gate and_gate_2 (.in_1(Load), .in_2(L_4), .out_3(and_gate_2_out_3));
  OR_Gate or_gate_1 (.in_1(and_gate_1_out_3), .in_2(and_gate_2_out_3), .out_3(out_11));
  AND_Gate and_gate_3 (.in_1(Increment), .in_2(H), .out_3(and_gate_3_out_3));
  AND_Gate and_gate_4 (.in_1(Load), .in_2(L), .out_3(and_gate_4_out_3));
  OR_Gate or_gate_2 (.in_1(and_gate_3_out_3), .in_2(and_gate_4_out_3), .out_3(out_12));
  AND_Gate and_gate_5 (.in_1(Increment), .in_2(H_2), .out_3(and_gate_5_out_3));
  AND_Gate and_gate_6 (.in_1(Load), .in_2(L_2), .out_3(and_gate_6_out_3));
  AND_Gate and_gate_7 (.in_1(Increment), .in_2(H_3), .out_3(and_gate_7_out_3));
  OR_Gate or_gate_3 (.in_1(and_gate_5_out_3), .in_2(and_gate_6_out_3), .out_3(out_13));
  AND_Gate and_gate_8 (.in_1(Load), .in_2(L_3), .out_3(and_gate_8_out_3));
  OR_Gate or_gate_4 (.in_1(and_gate_7_out_3), .in_2(and_gate_8_out_3), .out_3(out_14));
endmodule

// Incrementer
module Incrementer_4bit (
  input  in_1,
  input  in_2,
  input  in_3,
  input  in_4,
  output Overflow,
  output out_6,
  output out_7,
  output out_8,
  output out_9
);

  wire and_gate_2_out_3, and_gate_3_out_3, and_gate_4_out_3;

  AND_Gate and_gate_1 (.in_1(and_gate_2_out_3), .in_2(in_1), .out_3(Overflow));
  XOR xor_1 (.INPUT_1(and_gate_2_out_3), .INPUT_2(in_1), .OUT(out_6));
  AND_Gate and_gate_2 (.in_1(and_gate_3_out_3), .in_2(in_2), .out_3(and_gate_2_out_3));
  XOR xor_2 (.INPUT_1(and_gate_3_out_3), .INPUT_2(in_2), .OUT(out_7));
  AND_Gate and_gate_3 (.in_1(and_gate_4_out_3), .in_2(in_3), .out_3(and_gate_3_out_3));
  XOR xor_3 (.INPUT_1(and_gate_4_out_3), .INPUT_2(in_3), .OUT(out_8));
  AND_Gate and_gate_4 (.in_1(1'b1), .in_2(in_4), .out_3(and_gate_4_out_3));
  XOR xor_4 (.INPUT_1(1'b1), .INPUT_2(in_4), .OUT(out_9));
endmodule

module left_shift (
  input  [7:0] in_1,
  output [7:0] out_2,
  output out_3
);


  assign out_2 = {in_1[6:0], 1'b0};
  assign out_3 = in_1[7];
endmodule

module right_shift (
  input  [7:0] in_1,
  output out_2,
  output [7:0] out_3
);


  assign out_2 = in_1[0];
  assign out_3 = {1'b0, in_1[7:1]};
endmodule

// Sum
module ODD (
  input  A,
  input  B,
  input  in_3,
  output out_4
);

  wire xor_1_out;

  XOR xor_1 (.INPUT_1(A), .INPUT_2(B), .OUT(xor_1_out));
  XOR xor_2 (.INPUT_1(xor_1_out), .INPUT_2(in_3), .OUT(out_4));
endmodule

// Carry
module MAJ (
  input  A,
  input  B,
  input  C,
  output out_4
);

  wire and_gate_1_out_3, and_gate_2_out_3, and_gate_3_out_3, xor_1_out;

  AND_Gate and_gate_1 (.in_1(A), .in_2(B), .out_3(and_gate_1_out_3));
  AND_Gate and_gate_2 (.in_1(A), .in_2(C), .out_3(and_gate_2_out_3));
  AND_Gate and_gate_3 (.in_1(B), .in_2(C), .out_3(and_gate_3_out_3));
  XOR xor_1 (.INPUT_1(and_gate_1_out_3), .INPUT_2(and_gate_2_out_3), .OUT(xor_1_out));
  XOR xor_2 (.INPUT_1(xor_1_out), .INPUT_2(and_gate_3_out_3), .OUT(out_4));
endmodule

// NOT
module NOTGate (
  input  X,
  output Y
);

  Pull_Resistor pull_resistor_1 (.node(Y));
  Transistor transistor_1 (.in(1'b1), .out(Y), .gate(X));
endmodule

// AND
module AND_Gate (
  input  in_1,
  input  in_2,
  output out_3
);

  wire transistor_1_out;

  Pull_Resistor pull_resistor_1 (.node(in_1));
  Pull_Resistor pull_resistor_2 (.node(in_2));
  Transistor #(.\type ("n")) transistor_1 (.in(1'b1), .out(transistor_1_out), .gate(in_1));
  Transistor #(.\type ("n")) transistor_2 (.in(transistor_1_out), .out(out_3), .gate(in_2));
  Pull_Resistor pull_resistor_3 (.node(out_3));
endmodule

// OR
module OR_Gate (
  input  in_1,
  input  in_2,
  output out_3
);

  Pull_Resistor pull_resistor_1 (.node(in_1));
  Transistor #(.\type ("n")) transistor_1 (.in(1'b1), .out(out_3), .gate(in_1));
  Pull_Resistor pull_resistor_2 (.node(in_2));
  Transistor #(.\type ("n")) transistor_2 (.in(1'b1), .out(out_3), .gate(in_2));
  Pull_Resistor pull_resistor_3 (.node(out_3));
endmodule

module XOR (
  input  INPUT_1,
  input  INPUT_2,
  output OUT
);

  wire and_gate_1_out_3, and_gate_2_out_3, notgate_1_y, notgate_2_y;

  NOTGate notgate_1 (.Y(notgate_1_y), .X(INPUT_1));
  NOTGate notgate_2 (.Y(notgate_2_y), .X(INPUT_2));
  AND_Gate and_gate_1 (.in_1(notgate_1_y), .in_2(INPUT_2), .out_3(and_gate_1_out_3));
  AND_Gate and_gate_2 (.in_1(INPUT_1), .in_2(notgate_2_y), .out_3(and_gate_2_out_3));
  OR_Gate or_gate_1 (.in_1(and_gate_1_out_3), .in_2(and_gate_2_out_3), .out_3(OUT));

  // Notes on the sheet:
  //   NOT
  //   NOT
  //   AND
  //   AND
  //   OR
endmodule

module NAND (
  input  AND,
  input  in_2,
  output out_3
);

  wire and_gate_1_out_3;

  AND_Gate and_gate_1 (.in_1(AND), .in_2(in_2), .out_3(and_gate_1_out_3));
  NOTGate notgate_1 (.Y(out_3), .X(and_gate_1_out_3));

  // Notes on the sheet:
  //   NOT
endmodule

module NOR (
  input  in_1,
  input  in_2,
  output out_3
);

  wire nand_1_out_3, nand_2_out_3, nand_3_out_3;

  NAND nand_1 (.AND(in_1), .in_2(in_1), .out_3(nand_1_out_3));
  NAND nand_2 (.AND(in_2), .in_2(in_2), .out_3(nand_2_out_3));
  NAND nand_3 (.AND(nand_1_out_3), .in_2(nand_2_out_3), .out_3(nand_3_out_3));
  NAND nand_4 (.AND(nand_3_out_3), .in_2(nand_3_out_3), .out_3(out_3));

  // Notes on the sheet:
  //   NAND
  //   NAND
  //   NAND
  //   NAND
endmodule

module XNOR (
  input  in_1,
  input  in_2,
  output out_3
);

  wire and_gate_1_out_3, nor_1_out_3;

  NOR nor_1 (.in_1(in_1), .in_2(in_2), .out_3(nor_1_out_3));
  AND_Gate and_gate_1 (.in_1(in_2), .in_2(in_1), .out_3(and_gate_1_out_3));
  OR_Gate or_gate_1 (.in_1(nor_1_out_3), .in_2(and_gate_1_out_3), .out_3(out_3));

  // Notes on the sheet:
  //   NOR
  //   AND
  //   OR
endmodule

// OR
module _8_bit_OR (
  input  [7:0] in_1,
  input  [7:0] in_2,
  output [7:0] out_3
);

  OR_Gate or_gate_1 (.in_1(in_1[0]), .in_2(in_2[0]), .out_3(out_3[0]));
  OR_Gate or_gate_2 (.in_1(in_1[1]), .in_2(in_2[1]), .out_3(out_3[1]));
  OR_Gate or_gate_3 (.in_1(in_1[2]), .in_2(in_2[2]), .out_3(out_3[2]));
  OR_Gate or_gate_4 (.in_1(in_1[3]), .in_2(in_2[3]), .out_3(out_3[3]));
  OR_Gate or_gate_5 (.in_1(in_1[4]), .in_2(in_2[4]), .out_3(out_3[4]));
  OR_Gate or_gate_6 (.in_1(in_1[5]), .in_2(in_2[5]), .out_3(out_3[5]));
  OR_Gate or_gate_7 (.in_1(in_1[6]), .in_2(in_2[6]), .out_3(out_3[6]));
  OR_Gate or_gate_8 (.in_1(in_1[7]), .in_2(in_2[7]), .out_3(out_3[7]));
endmodule

// AND
module _8_bit_AND (
  input  [7:0] in_1,
  input  [7:0] in_2,
  output [7:0] out_3
);

  AND_Gate and_gate_1 (.in_1(in_1[0]), .in_2(in_2[0]), .out_3(out_3[0]));
  AND_Gate and_gate_2 (.in_1(in_1[1]), .in_2(in_2[1]), .out_3(out_3[1]));
  AND_Gate and_gate_3 (.in_1(in_1[2]), .in_2(in_2[2]), .out_3(out_3[2]));
  AND_Gate and_gate_4 (.in_1(in_1[3]), .in_2(in_2[3]), .out_3(out_3[3]));
  AND_Gate and_gate_5 (.in_1(in_1[4]), .in_2(in_2[4]), .out_3(out_3[4]));
  AND_Gate and_gate_6 (.in_1(in_1[5]), .in_2(in_2[5]), .out_3(out_3[5]));
  AND_Gate and_gate_7 (.in_1(in_1[6]), .in_2(in_2[6]), .out_3(out_3[6]));
  AND_Gate and_gate_8 (.in_1(in_1[7]), .in_2(in_2[7]), .out_3(out_3[7]));
endmodule

// XOR
module _8_bit_XOR (
  input  [7:0] in_1,
  input  [7:0] in_2,
  output [7:0] out_3
);

  XOR xor_1 (.INPUT_1(in_1[0]), .INPUT_2(in_2[0]), .OUT(out_3[0]));
  XOR xor_2 (.INPUT_1(in_1[1]), .INPUT_2(in_2[1]), .OUT(out_3[1]));
  XOR xor_3 (.INPUT_1(in_1[2]), .INPUT_2(in_2[2]), .OUT(out_3[2]));
  XOR xor_4 (.INPUT_1(in_1[3]), .INPUT_2(in_2[3]), .OUT(out_3[3]));
  XOR xor_5 (.INPUT_1(in_1[4]), .INPUT_2(in_2[4]), .OUT(out_3[4]));
  XOR xor_6 (.INPUT_1(in_1[5]), .INPUT_2(in_2[5]), .OUT(out_3[5]));
  XOR xor_7 (.INPUT_1(in_1[6]), .INPUT_2(in_2[6]), .OUT(out_3[6]));
  XOR xor_8 (.INPUT_1(in_1[7]), .INPUT_2(in_2[7]), .OUT(out_3[7]));
endmodule

// AND
module _9_And (
  input  in_1,
  input  [7:0] in_2,
  output [7:0] out_3
);

  AND_Gate and_gate_1 (.in_1(in_2[0]), .in_2(in_1), .out_3(out_3[0]));
  AND_Gate and_gate_2 (.in_1(in_2[1]), .in_2(in_1), .out_3(out_3[1]));
  AND_Gate and_gate_3 (.in_1(in_2[2]), .in_2(in_1), .out_3(out_3[2]));
  AND_Gate and_gate_4 (.in_1(in_2[3]), .in_2(in_1), .out_3(out_3[3]));
  AND_Gate and_gate_5 (.in_1(in_2[4]), .in_2(in_1), .out_3(out_3[4]));
  AND_Gate and_gate_6 (.in_1(in_2[5]), .in_2(in_1), .out_3(out_3[5]));
  AND_Gate and_gate_7 (.in_1(in_2[6]), .in_2(in_1), .out_3(out_3[6]));
  AND_Gate and_gate_8 (.in_1(in_2[7]), .in_2(in_1), .out_3(out_3[7]));
endmodule

module AND4 (
  input  in_1,
  input  in_2,
  input  in_3,
  input  in_4,
  output out_5
);

  wire transistor_1_out, transistor_2_out, transistor_3_out;

  Pull_Resistor pull_resistor_1 (.node(in_1));
  Pull_Resistor pull_resistor_2 (.node(in_2));
  Pull_Resistor pull_resistor_3 (.node(in_3));
  Pull_Resistor pull_resistor_4 (.node(in_4));
  Transistor #(.\type ("n")) transistor_1 (.in(1'b1), .out(transistor_1_out), .gate(in_1));
  Transistor #(.\type ("n")) transistor_2 (.in(transistor_1_out), .out(transistor_2_out), .gate(in_2));
  Transistor #(.\type ("n")) transistor_3 (.in(transistor_2_out), .out(transistor_3_out), .gate(in_3));
  Transistor #(.\type ("n")) transistor_4 (.in(transistor_3_out), .out(out_5), .gate(in_4));
  Pull_Resistor pull_resistor_5 (.node(out_5));
endmodule

// AND
module AND3 (
  input  in_1,
  input  in_2,
  input  in_3,
  output out_4
);

  wire transistor_1_out, transistor_2_out;

  Pull_Resistor pull_resistor_1 (.node(in_1));
  Pull_Resistor pull_resistor_2 (.node(in_2));
  Pull_Resistor pull_resistor_3 (.node(in_3));
  Transistor #(.\type ("n")) transistor_1 (.in(1'b1), .out(transistor_1_out), .gate(in_1));
  Transistor #(.\type ("n")) transistor_2 (.in(transistor_1_out), .out(transistor_2_out), .gate(in_2));
  Transistor #(.\type ("n")) transistor_3 (.in(transistor_2_out), .out(out_4), .gate(in_3));
  Pull_Resistor pull_resistor_4 (.node(out_4));
endmodule

// OR
module OR3 (
  input  in_1,
  input  in_2,
  input  in_3,
  output out_4
);

  Pull_Resistor pull_resistor_1 (.node(in_1));
  Transistor #(.\type ("n")) transistor_1 (.in(1'b1), .out(out_4), .gate(in_1));
  Pull_Resistor pull_resistor_2 (.node(in_2));
  Transistor #(.\type ("n")) transistor_2 (.in(1'b1), .out(out_4), .gate(in_2));
  Pull_Resistor pull_resistor_3 (.node(in_3));
  Transistor #(.\type ("n")) transistor_3 (.in(1'b1), .out(out_4), .gate(in_3));
  Pull_Resistor pull_resistor_4 (.node(out_4));
endmodule

module OR (
  input  [7:0] in_1,
  input  [7:0] in_2,
  input  [7:0] in_3,
  output [7:0] out_4
);

  OR3 or3_1 (.in_1(in_1[0]), .in_2(in_2[0]), .in_3(in_3[0]), .out_4(out_4[0]));
  OR3 or3_2 (.in_1(in_1[1]), .in_2(in_2[1]), .in_3(in_3[1]), .out_4(out_4[1]));
  OR3 or3_3 (.in_1(in_1[2]), .in_2(in_2[2]), .in_3(in_3[2]), .out_4(out_4[2]));
  OR3 or3_4 (.in_1(in_1[3]), .in_2(in_2[3]), .in_3(in_3[3]), .out_4(out_4[3]));
  OR3 or3_5 (.in_1(in_1[4]), .in_2(in_2[4]), .in_3(in_3[4]), .out_4(out_4[4]));
  OR3 or3_6 (.in_1(in_1[5]), .in_2(in_2[5]), .in_3(in_3[5]), .out_4(out_4[5]));
  OR3 or3_7 (.in_1(in_1[6]), .in_2(in_2[6]), .in_3(in_3[6]), .out_4(out_4[6]));
  OR3 or3_8 (.in_1(in_1[7]), .in_2(in_2[7]), .in_3(in_3[7]), .out_4(out_4[7]));
endmodule

module NOT_Small (
  input  X,
  output Y
);

  Pull_Resistor pull_resistor_1 (.node(Y));
  Transistor transistor_1 (.in(1'b1), .out(Y), .gate(X));
endmodule

module AND_gate_for_clock (
  input  in_1,
  input  in_2,
  output out_3
);

  wire notgate_1_y;

  NOTGate notgate_1 (.Y(notgate_1_y), .X(in_2));
  AND_Gate and_gate_1 (.in_1(in_1), .in_2(notgate_1_y), .out_3(out_3));
endmodule

// NOR
module _4_nor (
  input  in_1,
  input  in_2,
  input  in_3,
  input  in_4,
  output out_5
);

  wire transistor_1_out;

  Pull_Resistor pull_resistor_1 (.node(in_1));
  Transistor #(.\type ("n")) transistor_1 (.in(1'b1), .out(transistor_1_out), .gate(in_1));
  Pull_Resistor pull_resistor_2 (.node(in_2));
  Transistor #(.\type ("n")) transistor_2 (.in(1'b1), .out(transistor_1_out), .gate(in_2));
  Pull_Resistor pull_resistor_3 (.node(in_3));
  Transistor #(.\type ("n")) transistor_3 (.in(1'b1), .out(transistor_1_out), .gate(in_3));
  Pull_Resistor pull_resistor_4 (.node(in_4));
  Transistor #(.\type ("n")) transistor_4 (.in(1'b1), .out(transistor_1_out), .gate(in_4));
  Pull_Resistor pull_resistor_5 (.node(transistor_1_out));
  NOTGate notgate_1 (.Y(out_5), .X(transistor_1_out));
endmodule

module _5OR (
  input  in_1,
  input  in_2,
  input  in_3,
  input  in_4,
  input  in_5,
  output out_6
);

  Pull_Resistor pull_resistor_1 (.node(in_1));
  Transistor #(.\type ("n")) transistor_1 (.in(1'b1), .out(out_6), .gate(in_1));
  Pull_Resistor pull_resistor_2 (.node(in_2));
  Transistor #(.\type ("n")) transistor_2 (.in(1'b1), .out(out_6), .gate(in_2));
  Pull_Resistor pull_resistor_3 (.node(in_3));
  Transistor #(.\type ("n")) transistor_3 (.in(1'b1), .out(out_6), .gate(in_3));
  Pull_Resistor pull_resistor_4 (.node(in_4));
  Transistor #(.\type ("n")) transistor_4 (.in(1'b1), .out(out_6), .gate(in_4));
  Pull_Resistor pull_resistor_5 (.node(in_5));
  Transistor #(.\type ("n")) transistor_5 (.in(1'b1), .out(out_6), .gate(in_5));
  Pull_Resistor pull_resistor_6 (.node(out_6));
endmodule

// OR
module _16OR (
  input  [7:0] in_1,
  input  [7:0] in_2,
  input  [7:0] in_3,
  input  [7:0] in_4,
  input  [7:0] in_5,
  input  [7:0] in_6,
  input  [7:0] in_7,
  input  [7:0] in_8,
  input  [7:0] in_9,
  input  [7:0] in_10,
  input  [7:0] in_11,
  input  [7:0] in_12,
  input  [7:0] in_13,
  input  [7:0] in_14,
  input  [7:0] in_15,
  input  [7:0] in_16,
  output [7:0] out_17
);

  wire [7:0] n8_bit_or_1_out_3, n8_bit_or_2_out_3, n8_bit_or_3_out_3, n8_bit_or_4_out_3, n8_bit_or_5_out_3,
       n8_bit_or_6_out_3, n8_bit_or_7_out_3, n8_bit_or_8_out_3, n8_bit_or_9_out_3, n8_bit_or_10_out_3,
       n8_bit_or_11_out_3, n8_bit_or_12_out_3, n8_bit_or_13_out_3, n8_bit_or_14_out_3;

  _8_bit_OR u_8_bit_or_1 (.in_2(in_2), .out_3(n8_bit_or_1_out_3), .in_1(in_1));
  _8_bit_OR u_8_bit_or_2 (.in_2(in_4), .out_3(n8_bit_or_2_out_3), .in_1(in_3));
  _8_bit_OR u_8_bit_or_3 (.in_2(in_6), .out_3(n8_bit_or_3_out_3), .in_1(in_5));
  _8_bit_OR u_8_bit_or_4 (.in_2(in_8), .out_3(n8_bit_or_4_out_3), .in_1(in_7));
  _8_bit_OR u_8_bit_or_5 (.in_2(in_10), .out_3(n8_bit_or_5_out_3), .in_1(in_9));
  _8_bit_OR u_8_bit_or_6 (.in_2(in_12), .out_3(n8_bit_or_6_out_3), .in_1(in_11));
  _8_bit_OR u_8_bit_or_7 (.in_2(in_14), .out_3(n8_bit_or_7_out_3), .in_1(in_13));
  _8_bit_OR u_8_bit_or_8 (.in_2(in_16), .out_3(n8_bit_or_8_out_3), .in_1(in_15));
  _8_bit_OR u_8_bit_or_9 (.in_2(n8_bit_or_2_out_3), .out_3(n8_bit_or_9_out_3), .in_1(n8_bit_or_1_out_3));
  _8_bit_OR u_8_bit_or_10 (.in_2(n8_bit_or_4_out_3), .out_3(n8_bit_or_10_out_3), .in_1(n8_bit_or_3_out_3));
  _8_bit_OR u_8_bit_or_11 (.in_2(n8_bit_or_6_out_3), .out_3(n8_bit_or_11_out_3), .in_1(n8_bit_or_5_out_3));
  _8_bit_OR u_8_bit_or_12 (.in_2(n8_bit_or_8_out_3), .out_3(n8_bit_or_12_out_3), .in_1(n8_bit_or_7_out_3));
  _8_bit_OR u_8_bit_or_13 (.in_2(n8_bit_or_10_out_3), .out_3(n8_bit_or_13_out_3), .in_1(n8_bit_or_9_out_3));
  _8_bit_OR u_8_bit_or_14 (.in_2(n8_bit_or_12_out_3), .out_3(n8_bit_or_14_out_3), .in_1(n8_bit_or_11_out_3));
  _8_bit_OR u_8_bit_or_15 (.in_2(n8_bit_or_14_out_3), .out_3(out_17), .in_1(n8_bit_or_13_out_3));
endmodule

// 1-bit mem
module _1bit_mem_CORRECT (
  input  Data,
  input  Read_Write,
  output out_3
);

  wire and_1_out, and_2_out, clock_1_out, not_1_out;

  not not_1 (not_1_out, Data);
  and and_1 (and_1_out, Data, Read_Write);
  and and_2 (and_2_out, not_1_out, Read_Write);
  Clock_part clock_1 (.out(clock_1_out));
  S_R_Flip_Flop s_r_ff_1 (.S(and_1_out), .clk(clock_1_out), .R(and_2_out), .Q(out_3));  // open: Qn, preset, reset, en
endmodule

// Decider
module _8_bit_Decider (
  input  in_1,
  input  [7:0] in_2,
  input  [7:0] in_3,
  output [7:0] out_4
);

  wire not_small_1_y;
  wire [7:0] n9_and_1_out_3, n9_and_2_out_3;

  _9_And u_9_and_1 (.in_2(in_2), .out_3(n9_and_1_out_3), .in_1(in_1));
  NOT_Small not_small_1 (.Y(not_small_1_y), .X(in_1));
  _9_And u_9_and_2 (.in_2(in_3), .out_3(n9_and_2_out_3), .in_1(not_small_1_y));
  _8_bit_OR u_8_bit_or_1 (.in_2(n9_and_1_out_3), .out_3(out_4), .in_1(n9_and_2_out_3));
endmodule

// Decider
module _4_bit_Decider (
  input  [3:0] in_1,
  input  [3:0] in_2,
  input  in_3,
  output [3:0] out_4
);

  wire not_small_1_y;
  wire [3:0] n5_and_1_out_3, n5_and_2_out_3;

  _5_And u_5_and_1 (.in_2(in_1), .out_3(n5_and_1_out_3), .in_1(in_3));
  _4_bit_OR u_4_bit_or_1 (.in_2(n5_and_1_out_3), .in_1(n5_and_2_out_3), .out_3(out_4));
  NOT_Small not_small_1 (.Y(not_small_1_y), .X(in_3));
  _5_And u_5_and_2 (.in_2(in_2), .out_3(n5_and_2_out_3), .in_1(not_small_1_y));
endmodule

// AND
module _5_And (
  input  in_1,
  input  [3:0] in_2,
  output [3:0] out_3
);

  AND_Gate and_gate_1 (.in_1(in_2[0]), .in_2(in_1), .out_3(out_3[0]));
  AND_Gate and_gate_2 (.in_1(in_2[1]), .in_2(in_1), .out_3(out_3[1]));
  AND_Gate and_gate_3 (.in_1(in_2[2]), .in_2(in_1), .out_3(out_3[2]));
  AND_Gate and_gate_4 (.in_1(in_2[3]), .in_2(in_1), .out_3(out_3[3]));
endmodule

// OR
module _4_bit_OR (
  input  [3:0] in_1,
  input  [3:0] in_2,
  output [3:0] out_3
);

  OR_Gate or_gate_1 (.in_1(in_2[3]), .in_2(in_1[3]), .out_3(out_3[3]));
  OR_Gate or_gate_2 (.in_1(in_2[2]), .in_2(in_1[2]), .out_3(out_3[2]));
  OR_Gate or_gate_3 (.in_1(in_2[1]), .in_2(in_1[1]), .out_3(out_3[1]));
  OR_Gate or_gate_4 (.in_1(in_2[0]), .in_2(in_1[0]), .out_3(out_3[0]));
endmodule

// Dec
module _1_bit_Decider (
  input  in_1,
  input  in_2,
  input  in_3,
  output out_4
);

  wire and_gate_1_out_3, and_gate_2_out_3, not_small_1_y;

  AND_Gate and_gate_1 (.in_1(in_3), .in_2(in_1), .out_3(and_gate_1_out_3));
  OR_Gate or_gate_1 (.in_1(and_gate_2_out_3), .in_2(and_gate_1_out_3), .out_3(out_4));
  NOT_Small not_small_1 (.Y(not_small_1_y), .X(in_3));
  AND_Gate and_gate_2 (.in_1(not_small_1_y), .in_2(in_2), .out_3(and_gate_2_out_3));
endmodule
